# Fritzing sketch led-series (saved by Fritzing 1.0.1)

parts:
  J1 = J1 5V input [value="5V input" package=header]
  R1 = R1 330 ohm [value="330 ohm" package=resistor]
  D1 = D1 Red LED [value="Red LED" package=led]

nets:
  N1: J1.5V, R1.1
  N2: J1.GND, D1.K
  N3: R1.2, D1.A

custom parts:
  J1 5V input: Explicit user-defined through-hole footprint; verify against component datasheet.
  R1 330 ohm: Explicit user-defined through-hole footprint; verify against component datasheet.
  D1 Red LED: Explicit user-defined through-hole footprint; verify against component datasheet.
